// Logisim project Calculadora_4bits.circ as structural Verilog: 9 circuits, main circuit Calculadora
module Calculadora (
  input  a3,
  input  a2,
  input  a1,
  input  a0,
  input  b3,
  input  b2,
  input  b1,
  input  b0,
  input  [1:0] in_9,
  output [7:0] out_10,
  output out_11,
  output [3:0] out_12
);

  wire A1_t, B1_t, C_a, C_b, C_c, C_d, C_e, C_f, C_g, D_a, D_b, D_c, D_d, D_e, D_f, D_g, LIMPAR_out, U_a,
       U_b, U_c, U_d, U_e, U_f, U_g;
  wire [3:0] A_ALTERNATIVO, conversor_1_centena, conversor_1_dezena, conversor_1_unidade,
       divisor2_1_quociente;
  wire [7:0] bit_extender_1_out, bit_extender_2_out, multiplicador_1_res_mult, register_1_q,
       somador_4_bits_1_res_soma, subtrator_1_res_sub;
  wire [7:4] multiplexer_2_out;

  _7_Segment_Display u_7_segment_display_1 (.g(C_g), .f(C_f), .a(C_a), .b(C_b), .e(C_e), .d(C_d), .c(C_c));  // open: dp
  _7_Segment_Display u_7_segment_display_2 (.g(D_g), .f(D_f), .a(D_a), .b(D_b), .e(D_e), .d(D_d), .c(D_c));  // open: dp
  _7_Segment_Display u_7_segment_display_3 (.g(U_g), .f(U_f), .a(U_a), .b(U_b), .e(U_e), .d(U_d), .c(U_c));  // open: dp
  SOMADOR_4_bits somador_4_bits_1 (
    .a0(A_ALTERNATIVO[0]), .a1(A_ALTERNATIVO[1]), .a2(A_ALTERNATIVO[2]), .a3(A_ALTERNATIVO[3]), .b0(b0),
    .b1(b1), .b2(b2), .b3(b3), .RES_SOMA(somador_4_bits_1_res_soma));
  SUBTRATOR subtrator_1 (
    .a0(A_ALTERNATIVO[0]), .a1(A_ALTERNATIVO[1]), .a2(A_ALTERNATIVO[2]), .a3(A_ALTERNATIVO[3]), .b0(b0),
    .b1(b1), .b2(b2), .b3(b3), .RES_SUB(subtrator_1_res_sub), .Borrow(out_11));
  MULTIPLICADOR multiplicador_1 (
    .a3(A_ALTERNATIVO[3]), .a2(A_ALTERNATIVO[2]), .a1(A_ALTERNATIVO[1]), .a0(A_ALTERNATIVO[0]), .b0(b0),
    .b1(b1), .b2(b2), .b3(b3), .RES_MULT(multiplicador_1_res_mult));
  DIVISOR2 divisor2_1 (
    .DIVIDENDO(A_ALTERNATIVO), .DIVISOR({b3, b2, b1, b0}), .quociente(divisor2_1_quociente), .RESTO(out_12));
  assign bit_extender_1_out = {{4{1'b0}}, divisor2_1_quociente};  // Bit_Extender bit_extender_1
  Button SALVAR_NUMERO (.out(A1_t));
  Button USAR_MEMORIA (.out(B1_t));
  Multiplexer #(.select(2), .width(8)) multiplexer_1 (
    .in0(somador_4_bits_1_res_soma), .in1(subtrator_1_res_sub), .in2(multiplicador_1_res_mult),
    .in3(bit_extender_1_out), .out(out_10), .sel(in_9));
  Register register_1 (.D(out_10), .clk(A1_t), .Q(register_1_q), .clr(LIMPAR_out));  // open: en
  Button LIMPAR (.out(LIMPAR_out));
  assign bit_extender_2_out = {{4{1'b0}}, {a3, a2, a1, a0}};  // Bit_Extender bit_extender_2
  Multiplexer #(.width(8)) multiplexer_2 (
    .in0(bit_extender_2_out), .in1(register_1_q), .out({multiplexer_2_out, A_ALTERNATIVO}), .sel(B1_t));
  CONVERSOR conversor_1 (
    .RESULTADO(out_10), .UNIDADE(conversor_1_unidade), .CENTENA(conversor_1_centena),
    .DEZENA(conversor_1_dezena));
  DECODIFICADOR_BCD decodificador_bcd_1 (
    .BCD(conversor_1_unidade), .a(U_a), .b(U_b), .c(U_c), .d(U_d), .e(U_e), .f(U_f), .g(U_g));
  DECODIFICADOR_BCD decodificador_bcd_2 (
    .BCD(conversor_1_centena), .a(C_a), .b(C_b), .c(C_c), .d(C_d), .e(C_e), .f(C_f), .g(C_g));
  DECODIFICADOR_BCD decodificador_bcd_3 (
    .BCD(conversor_1_dezena), .a(D_a), .b(D_b), .c(D_c), .d(D_d), .e(D_e), .f(D_f), .g(D_g));

  // Notes on the sheet:
  //   DIV - 11
  //   SOMA - 00
  //   SUB - 01
  //   MULT - 10
endmodule

module FULL_ADDER (
  input  A,
  input  B,
  input  CIN,
  output SUM,
  output COUT
);

  wire and_1_out, and_2_out, and_3_out, xor_1_out;

  xor xor_1 (xor_1_out, A, B);
  and and_1 (and_1_out, A, B);
  and and_2 (and_2_out, A, CIN);
  and and_3 (and_3_out, CIN, B);
  xor xor_2 (SUM, xor_1_out, CIN);
  or or_1 (COUT, and_1_out, and_2_out, and_3_out);
endmodule

module SUBTRATOR (
  input  a0,
  input  a1,
  input  a2,
  input  a3,
  input  b0,
  input  b1,
  input  b2,
  input  b3,
  output [7:0] RES_SUB,
  output Borrow
);

  wire full_adder_1_cout, full_adder_2_cout, full_adder_3_cout, xor_1_out, xor_2_out, xor_3_out, xor_4_out;

  xor xor_1 (xor_1_out, 1'b1, b0);
  xor xor_2 (xor_2_out, 1'b1, b1);
  xor xor_3 (xor_3_out, 1'b1, b2);
  xor xor_4 (xor_4_out, 1'b1, b3);
  FULL_ADDER full_adder_1 (.A(a0), .B(xor_1_out), .CIN(1'b1), .SUM(RES_SUB[0]), .COUT(full_adder_1_cout));
  FULL_ADDER full_adder_2 (.A(a1), .B(xor_2_out), .CIN(full_adder_1_cout), .SUM(RES_SUB[1]), .COUT(full_adder_2_cout));
  FULL_ADDER full_adder_3 (.A(a2), .B(xor_3_out), .CIN(full_adder_2_cout), .SUM(RES_SUB[2]), .COUT(full_adder_3_cout));
  FULL_ADDER full_adder_4 (.A(a3), .B(xor_4_out), .CIN(full_adder_3_cout), .SUM(RES_SUB[3]), .COUT(Borrow));
endmodule

module MULTIPLICADOR (
  input  a3,
  input  a2,
  input  a1,
  input  a0,
  input  b0,
  input  b1,
  input  b2,
  input  b3,
  output [7:0] RES_MULT
);

  wire not_2_out, not_3_out, not_4_out;
  wire [3:0] adder_1_out, adder_2_out, and_4_out, and_8_out, and_12_out, and_15_out;

  and and_1 (and_4_out[3], b3, a3);
  and and_2 (and_4_out[2], b3, a2);
  and and_3 (and_4_out[1], b3, a1);
  and and_4 (and_4_out[0], b3, a0);
  and and_5 (and_8_out[3], b2, a3);
  and and_6 (and_8_out[2], b2, a2);
  and and_7 (and_8_out[1], b2, a1);
  and and_8 (and_8_out[0], b2, a0);
  and and_9 (and_12_out[3], b1, a3);
  and and_10 (and_12_out[2], b1, a2);
  and and_11 (and_12_out[1], b1, a1);
  and and_12 (and_12_out[0], b1, a0);
  and and_13 (and_15_out[2], b0, a3);
  and and_14 (and_15_out[1], b0, a2);
  not not_1 (and_15_out[3], 1'b1);
  and and_15 (and_15_out[0], b0, a1);
  and and_16 (RES_MULT[0], b0, a0);
  not not_2 (not_2_out, 1'b1);
  Adder #(.width(4)) adder_1 (
    .a(and_15_out), .b(and_12_out), .out({adder_1_out[2:0], RES_MULT[1]}), .cin(not_2_out),
    .cout(adder_1_out[3]));
  not not_3 (not_3_out, 1'b1);
  Adder #(.width(4)) adder_2 (
    .a(adder_1_out), .b(and_8_out), .out({adder_2_out[2:0], RES_MULT[2]}), .cin(not_3_out),
    .cout(adder_2_out[3]));
  not not_4 (not_4_out, 1'b1);
  Adder #(.width(4)) adder_3 (.a(adder_2_out), .b(and_4_out), .out(RES_MULT[6:3]), .cin(not_4_out), .cout(RES_MULT[7]));
endmodule

module SOMADOR_4_bits (
  input  a0,
  input  a1,
  input  a2,
  input  a3,
  input  b0,
  input  b1,
  input  b2,
  input  b3,
  output [7:0] RES_SOMA
);

  wire full_adder_1_cout, full_adder_2_cout, full_adder_3_cout, xor_1_out, xor_2_out, xor_3_out, xor_4_out;

  xor xor_1 (xor_1_out, 1'b0, b0);
  xor xor_2 (xor_2_out, 1'b0, b1);
  xor xor_3 (xor_3_out, 1'b0, b2);
  xor xor_4 (xor_4_out, 1'b0, b3);
  FULL_ADDER full_adder_1 (.A(a0), .B(xor_1_out), .CIN(1'b0), .SUM(RES_SOMA[0]), .COUT(full_adder_1_cout));
  FULL_ADDER full_adder_2 (.A(a1), .B(xor_2_out), .CIN(full_adder_1_cout), .SUM(RES_SOMA[1]), .COUT(full_adder_2_cout));
  FULL_ADDER full_adder_3 (.A(a2), .B(xor_3_out), .CIN(full_adder_2_cout), .SUM(RES_SOMA[2]), .COUT(full_adder_3_cout));
  FULL_ADDER full_adder_4 (.A(a3), .B(xor_4_out), .CIN(full_adder_3_cout), .SUM(RES_SOMA[3]), .COUT(RES_SOMA[4]));
endmodule

module DIVISOR2 (
  input  [3:0] DIVIDENDO,
  input  [3:0] DIVISOR,
  output [3:0] quociente,
  output [3:0] RESTO
);

  wire estagio_divisor_1_ok, estagio_divisor_2_ok, estagio_divisor_3_ok, estagio_divisor_4_ok,
       estagio_divisor_5_ok, estagio_divisor_6_ok, estagio_divisor_7_ok, estagio_divisor_8_ok,
       estagio_divisor_9_ok, estagio_divisor_10_ok, estagio_divisor_11_ok, estagio_divisor_12_ok,
       estagio_divisor_13_ok, estagio_divisor_14_ok, estagio_divisor_15_ok;
  wire [3:0] adder_1_out, adder_2_out, adder_3_out, adder_4_out, adder_5_out, adder_6_out, adder_7_out,
       adder_8_out, adder_9_out, adder_10_out, adder_11_out, adder_12_out, adder_13_out, adder_14_out,
       bit_extender_1_out, bit_extender_2_out, bit_extender_3_out, bit_extender_4_out, bit_extender_5_out,
       bit_extender_6_out, bit_extender_7_out, bit_extender_8_out, bit_extender_9_out, bit_extender_10_out,
       bit_extender_11_out, bit_extender_12_out, bit_extender_13_out, bit_extender_14_out,
       bit_extender_15_out, estagio_divisor_1_saida, estagio_divisor_2_saida, estagio_divisor_3_saida,
       estagio_divisor_4_saida, estagio_divisor_5_saida, estagio_divisor_6_saida, estagio_divisor_7_saida,
       estagio_divisor_8_saida, estagio_divisor_9_saida, estagio_divisor_10_saida, estagio_divisor_11_saida,
       estagio_divisor_12_saida, estagio_divisor_13_saida, estagio_divisor_14_saida;

  Comparator #(.mode("unsigned"), .width(4)) comparator_1 (.a(DIVISOR), .b(4'b0000));  // open: gt, eq, lt
  ESTAGIO_DIVISOR estagio_divisor_1 (
    .ENTRADA(DIVIDENDO), .DIVISOR(DIVISOR), .ok(estagio_divisor_1_ok), .SAIDA(estagio_divisor_1_saida));
  assign bit_extender_1_out = {{3{1'b0}}, estagio_divisor_1_ok};  // Bit_Extender bit_extender_1
  ESTAGIO_DIVISOR estagio_divisor_2 (
    .ENTRADA(estagio_divisor_1_saida), .DIVISOR(DIVISOR), .ok(estagio_divisor_2_ok),
    .SAIDA(estagio_divisor_2_saida));
  assign bit_extender_2_out = {{3{1'b0}}, estagio_divisor_2_ok};  // Bit_Extender bit_extender_2
  Adder #(.width(4)) adder_1 (
    .a(bit_extender_1_out), .b(bit_extender_2_out), .out(adder_1_out), .cin(1'b0));  // open: cout
  ESTAGIO_DIVISOR estagio_divisor_3 (
    .ENTRADA(estagio_divisor_2_saida), .DIVISOR(DIVISOR), .ok(estagio_divisor_3_ok),
    .SAIDA(estagio_divisor_3_saida));
  assign bit_extender_3_out = {{3{1'b0}}, estagio_divisor_3_ok};  // Bit_Extender bit_extender_3
  ESTAGIO_DIVISOR estagio_divisor_4 (
    .ENTRADA(estagio_divisor_3_saida), .DIVISOR(DIVISOR), .ok(estagio_divisor_4_ok),
    .SAIDA(estagio_divisor_4_saida));
  assign bit_extender_4_out = {{3{1'b0}}, estagio_divisor_4_ok};  // Bit_Extender bit_extender_4
  Adder #(.width(4)) adder_2 (
    .a(bit_extender_3_out), .b(bit_extender_4_out), .out(adder_2_out), .cin(1'b0));  // open: cout
  ESTAGIO_DIVISOR estagio_divisor_5 (
    .ENTRADA(estagio_divisor_4_saida), .DIVISOR(DIVISOR), .ok(estagio_divisor_5_ok),
    .SAIDA(estagio_divisor_5_saida));
  Adder #(.width(4)) adder_3 (.a(adder_1_out), .b(adder_2_out), .out(adder_3_out), .cin(1'b0));  // open: cout
  assign bit_extender_5_out = {{3{1'b0}}, estagio_divisor_5_ok};  // Bit_Extender bit_extender_5
  ESTAGIO_DIVISOR estagio_divisor_6 (
    .ENTRADA(estagio_divisor_5_saida), .DIVISOR(DIVISOR), .ok(estagio_divisor_6_ok),
    .SAIDA(estagio_divisor_6_saida));
  assign bit_extender_6_out = {{3{1'b0}}, estagio_divisor_6_ok};  // Bit_Extender bit_extender_6
  Adder #(.width(4)) adder_4 (
    .a(bit_extender_5_out), .b(bit_extender_6_out), .out(adder_4_out), .cin(1'b0));  // open: cout
  ESTAGIO_DIVISOR estagio_divisor_7 (
    .ENTRADA(estagio_divisor_6_saida), .DIVISOR(DIVISOR), .ok(estagio_divisor_7_ok),
    .SAIDA(estagio_divisor_7_saida));
  assign bit_extender_7_out = {{3{1'b0}}, estagio_divisor_7_ok};  // Bit_Extender bit_extender_7
  ESTAGIO_DIVISOR estagio_divisor_8 (
    .ENTRADA(estagio_divisor_7_saida), .DIVISOR(DIVISOR), .ok(estagio_divisor_8_ok),
    .SAIDA(estagio_divisor_8_saida));
  assign bit_extender_8_out = {{3{1'b0}}, estagio_divisor_8_ok};  // Bit_Extender bit_extender_8
  Adder #(.width(4)) adder_5 (
    .a(bit_extender_7_out), .b(bit_extender_8_out), .out(adder_5_out), .cin(1'b0));  // open: cout
  ESTAGIO_DIVISOR estagio_divisor_9 (
    .ENTRADA(estagio_divisor_8_saida), .DIVISOR(DIVISOR), .ok(estagio_divisor_9_ok),
    .SAIDA(estagio_divisor_9_saida));
  assign bit_extender_9_out = {{3{1'b0}}, estagio_divisor_9_ok};  // Bit_Extender bit_extender_9
  Adder #(.width(4)) adder_6 (.a(adder_4_out), .b(adder_5_out), .out(adder_6_out), .cin(1'b0));  // open: cout
  ESTAGIO_DIVISOR estagio_divisor_10 (
    .ENTRADA(estagio_divisor_9_saida), .DIVISOR(DIVISOR), .ok(estagio_divisor_10_ok),
    .SAIDA(estagio_divisor_10_saida));
  assign bit_extender_10_out = {{3{1'b0}}, estagio_divisor_10_ok};  // Bit_Extender bit_extender_10
  Adder #(.width(4)) adder_7 (
    .a(bit_extender_9_out), .b(bit_extender_10_out), .out(adder_7_out), .cin(1'b0));  // open: cout
  assign bit_extender_11_out = {{3{1'b0}}, estagio_divisor_11_ok};  // Bit_Extender bit_extender_11
  ESTAGIO_DIVISOR estagio_divisor_11 (
    .ENTRADA(estagio_divisor_10_saida), .DIVISOR(DIVISOR), .ok(estagio_divisor_11_ok),
    .SAIDA(estagio_divisor_11_saida));
  ESTAGIO_DIVISOR estagio_divisor_12 (
    .ENTRADA(estagio_divisor_11_saida), .DIVISOR(DIVISOR), .ok(estagio_divisor_12_ok),
    .SAIDA(estagio_divisor_12_saida));
  assign bit_extender_12_out = {{3{1'b0}}, estagio_divisor_12_ok};  // Bit_Extender bit_extender_12
  Adder #(.width(4)) adder_8 (
    .a(bit_extender_11_out), .b(bit_extender_12_out), .out(adder_8_out), .cin(1'b0));  // open: cout
  ESTAGIO_DIVISOR estagio_divisor_13 (
    .ENTRADA(estagio_divisor_12_saida), .DIVISOR(DIVISOR), .ok(estagio_divisor_13_ok),
    .SAIDA(estagio_divisor_13_saida));
  Adder #(.width(4)) adder_9 (.a(adder_7_out), .b(adder_8_out), .out(adder_9_out), .cin(1'b0));  // open: cout
  assign bit_extender_13_out = {{3{1'b0}}, estagio_divisor_13_ok};  // Bit_Extender bit_extender_13
  ESTAGIO_DIVISOR estagio_divisor_14 (
    .ENTRADA(estagio_divisor_13_saida), .DIVISOR(DIVISOR), .ok(estagio_divisor_14_ok),
    .SAIDA(estagio_divisor_14_saida));
  Adder #(.width(4)) adder_10 (.a(adder_3_out), .b(adder_6_out), .out(adder_10_out), .cin(1'b0));  // open: cout
  Adder #(.width(4)) adder_11 (.a(adder_9_out), .b(adder_13_out), .out(adder_11_out), .cin(1'b0));  // open: cout
  assign bit_extender_14_out = {{3{1'b0}}, estagio_divisor_14_ok};  // Bit_Extender bit_extender_14
  Adder #(.width(4)) adder_12 (
    .a(bit_extender_13_out), .b(bit_extender_14_out), .out(adder_12_out), .cin(1'b0));  // open: cout
  ESTAGIO_DIVISOR estagio_divisor_15 (
    .ENTRADA(estagio_divisor_14_saida), .DIVISOR(DIVISOR), .ok(estagio_divisor_15_ok), .SAIDA(RESTO));
  Adder #(.width(4)) adder_13 (.a(adder_12_out), .b(4'b0000), .out(adder_13_out), .cin(1'b0));  // open: cout
  assign bit_extender_15_out = {{3{1'b0}}, estagio_divisor_15_ok};  // Bit_Extender bit_extender_15
  Adder #(.width(4)) adder_14 (.a(adder_10_out), .b(adder_11_out), .out(adder_14_out), .cin(1'b0));  // open: cout
  Adder #(.width(4)) adder_15 (.a(adder_14_out), .b(bit_extender_15_out), .out(quociente), .cin(1'b0));  // open: cout
endmodule

module CONVERSOR (
  input  [7:0] RESULTADO,
  output [3:0] UNIDADE,
  output [3:0] CENTENA,
  output [3:0] DEZENA
);

  wire comparator_1_eq, comparator_1_gt, comparator_2_eq, comparator_2_gt, comparator_3_eq, comparator_3_gt,
       comparator_4_eq, comparator_4_gt, comparator_5_eq, comparator_5_gt, comparator_6_eq, comparator_6_gt,
       comparator_7_eq, comparator_7_gt, comparator_8_eq, comparator_8_gt, comparator_9_eq, comparator_9_gt,
       comparator_10_eq, comparator_10_gt, comparator_11_eq, comparator_11_gt, GE10_out, GE20_out, GE30_out,
       GE40_out, GE50_out, GE60_out, GE70_out, GE80_out, GE90_out, GE100_out, GE200_out;
  wire [3:0] multiplexer_1_out, multiplexer_5_out, multiplexer_6_out, multiplexer_7_out, multiplexer_8_out,
       multiplexer_9_out, multiplexer_10_out, multiplexer_11_out, multiplexer_12_out;
  wire [7:0] bit_extender_1_out, multiplexer_2_out, multiplexer_3_out, multiplier_1_out, subtractor_1_out,
       subtractor_2_out;
  wire [7:4] subtractor_3_out;

  Comparator #(.mode("unsigned")) comparator_1 (
    .a(RESULTADO), .b(8'hc8), .gt(comparator_1_gt), .eq(comparator_1_eq));  // open: lt
  Comparator #(.mode("unsigned")) comparator_2 (
    .a(RESULTADO), .b(8'h64), .gt(comparator_2_gt), .eq(comparator_2_eq));  // open: lt
  or GE200 (GE200_out, comparator_1_gt, comparator_1_eq);
  or GE100 (GE100_out, comparator_2_gt, comparator_2_eq);
  Subtractor subtractor_1 (.a(RESULTADO), .b(8'h64), .out(subtractor_1_out));  // open: bin, bout
  Subtractor subtractor_2 (.a(RESULTADO), .b(8'hc8), .out(subtractor_2_out));  // open: bin, bout
  Multiplexer #(.width(4)) multiplexer_1 (.in0(4'b0000), .in1(4'b0001), .out(multiplexer_1_out), .sel(GE100_out));
  Multiplexer #(.width(8)) multiplexer_2 (
    .in0(RESULTADO), .in1(subtractor_1_out), .out(multiplexer_2_out), .sel(GE100_out));
  Multiplexer #(.width(8)) multiplexer_3 (
    .in0(multiplexer_2_out), .in1(subtractor_2_out), .out(multiplexer_3_out), .sel(GE200_out));
  Multiplexer #(.width(4)) multiplexer_4 (.in0(multiplexer_1_out), .in1(4'b0010), .out(CENTENA), .sel(GE200_out));
  Comparator #(.mode("unsigned")) comparator_3 (
    .a(multiplexer_3_out), .b(8'ha), .gt(comparator_3_gt), .eq(comparator_3_eq));  // open: lt
  Comparator #(.mode("unsigned")) comparator_4 (
    .a(multiplexer_3_out), .b(8'h14), .gt(comparator_4_gt), .eq(comparator_4_eq));  // open: lt
  Comparator #(.mode("unsigned")) comparator_5 (
    .a(multiplexer_3_out), .b(8'h1e), .gt(comparator_5_gt), .eq(comparator_5_eq));  // open: lt
  Comparator #(.mode("unsigned")) comparator_6 (
    .a(multiplexer_3_out), .b(8'h28), .gt(comparator_6_gt), .eq(comparator_6_eq));  // open: lt
  Comparator #(.mode("unsigned")) comparator_7 (
    .a(multiplexer_3_out), .b(8'h32), .gt(comparator_7_gt), .eq(comparator_7_eq));  // open: lt
  Comparator #(.mode("unsigned")) comparator_8 (
    .a(multiplexer_3_out), .b(8'h3c), .gt(comparator_8_gt), .eq(comparator_8_eq));  // open: lt
  Comparator #(.mode("unsigned")) comparator_9 (
    .a(multiplexer_3_out), .b(8'h46), .gt(comparator_9_gt), .eq(comparator_9_eq));  // open: lt
  Comparator #(.mode("unsigned")) comparator_10 (
    .a(multiplexer_3_out), .b(8'h50), .gt(comparator_10_gt), .eq(comparator_10_eq));  // open: lt
  Comparator #(.mode("unsigned")) comparator_11 (
    .a(multiplexer_3_out), .b(8'h5a), .gt(comparator_11_gt), .eq(comparator_11_eq));  // open: lt
  or GE10 (GE10_out, comparator_3_gt, comparator_3_eq);
  or GE20 (GE20_out, comparator_4_gt, comparator_4_eq);
  or GE30 (GE30_out, comparator_5_gt, comparator_5_eq);
  or GE40 (GE40_out, comparator_6_gt, comparator_6_eq);
  or GE50 (GE50_out, comparator_7_gt, comparator_7_eq);
  or GE60 (GE60_out, comparator_8_gt, comparator_8_eq);
  or GE70 (GE70_out, comparator_9_gt, comparator_9_eq);
  or GE80 (GE80_out, comparator_10_gt, comparator_10_eq);
  or GE90 (GE90_out, comparator_11_gt, comparator_11_eq);
  Multiplexer #(.width(4)) multiplexer_5 (.in0(4'b0000), .in1(4'b0001), .out(multiplexer_5_out), .sel(GE10_out));
  Multiplexer #(.width(4)) multiplexer_6 (
    .in0(multiplexer_5_out), .in1(4'b0010), .out(multiplexer_6_out), .sel(GE20_out));
  Multiplexer #(.width(4)) multiplexer_7 (
    .in0(multiplexer_6_out), .in1(4'b0011), .out(multiplexer_7_out), .sel(GE30_out));
  Multiplexer #(.width(4)) multiplexer_8 (
    .in0(multiplexer_7_out), .in1(4'b0100), .out(multiplexer_8_out), .sel(GE40_out));
  Multiplexer #(.width(4)) multiplexer_9 (
    .in0(multiplexer_8_out), .in1(4'b0101), .out(multiplexer_9_out), .sel(GE50_out));
  Multiplexer #(.width(4)) multiplexer_10 (
    .in0(multiplexer_9_out), .in1(4'b0110), .out(multiplexer_10_out), .sel(GE60_out));
  Multiplexer #(.width(4)) multiplexer_11 (
    .in0(multiplexer_10_out), .in1(4'b0111), .out(multiplexer_11_out), .sel(GE70_out));
  Multiplexer #(.width(4)) multiplexer_12 (
    .in0(multiplexer_11_out), .in1(4'b1000), .out(multiplexer_12_out), .sel(GE80_out));
  Multiplexer #(.width(4)) multiplexer_13 (.in0(multiplexer_12_out), .in1(4'b1001), .out(DEZENA), .sel(GE90_out));
  assign bit_extender_1_out = {{4{DEZENA[3]}}, DEZENA};  // Bit_Extender bit_extender_1
  Multiplier multiplier_1 (.a(bit_extender_1_out), .b(8'ha), .out(multiplier_1_out));  // open: cin, cout
  Subtractor subtractor_3 (
    .a(multiplexer_3_out), .b(multiplier_1_out), .out({subtractor_3_out, UNIDADE}));  // open: bin, bout

  // Notes on the sheet:
  //   CIRCUITO PARA RESTO
  //   CIRCUITO CONVERSOR CENTENA
  //   RESTO
  //   CIRCUITO CONVERSOR DEZENA
  //   CIRCUITO DE UNIDADE
endmodule

module DECODIFICADOR_BCD (
  input  [3:0] BCD,
  output a,
  output b,
  output c,
  output d,
  output e,
  output f,
  output g
);

  ROM #(.addrWidth(4), .dataWidth(7)) rom_1 (.addr(BCD), .data({a, b, c, d, e, f, g}));

  // Notes on the sheet:
  //   contents of rom_1 (hex, n*v repeats v):
  //   7e 30 6d 79 33 5b 5f 70 7f 7b
endmodule

module ESTAGIO_DIVISOR (
  input  [3:0] ENTRADA,
  input  [3:0] DIVISOR,
  output ok,
  output [3:0] SAIDA
);

  wire comparator_1_eq, comparator_1_gt;
  wire [3:0] subtractor_1_out;

  Subtractor #(.width(4)) subtractor_1 (.a(ENTRADA), .b(DIVISOR), .out(subtractor_1_out));  // open: bin, bout
  Comparator #(.mode("unsigned"), .width(4)) comparator_1 (
    .a(ENTRADA), .b(DIVISOR), .gt(comparator_1_gt), .eq(comparator_1_eq));  // open: lt
  or or_1 (ok, comparator_1_gt, comparator_1_eq);
  Multiplexer #(.width(4)) multiplexer_1 (.in0(ENTRADA), .in1(subtractor_1_out), .out(SAIDA), .sel(ok));

  // Notes on the sheet:
  //   Sub
  //   OK
  //   SAÍDA
endmodule
